// Logisim project Primeiro.circ as structural Verilog: 6 circuits, main circuit ULA
module main (
  input  Reset
);

  wire and_1_out, clock_1_out, clock_2_out, controlled_buffer_1_out, uc_1_b2, uc_1_cont, uc_1_grav, uc_1_mux1;
  wire [3:0] Contador_q, multiplexer_1_out, R_intr_q, RDM_q, REM_q;
  wire [7:0] caminho_de_datdos_que_eu_htendi_1_saida_para_o_pc, ram_1_data, register_1_q;
  wire [7:4] R_intr_q_2;

  assign controlled_buffer_1_out = uc_1_cont ? clock_1_out : 1'bz;  // Controlled_Buffer controlled_buffer_1
  Clock clock_1 (.out(clock_1_out));
  Clock clock_2 (.out(clock_2_out));
  Counter #(.width(4), .max('hf)) Contador (
    .Q(Contador_q), .clk(controlled_buffer_1_out), .clr(Reset));  // open: load, D, count, carry
  Register #(.width(4)) REM (.D(Contador_q), .Q(REM_q), .clk(clock_2_out), .clr(Reset));  // open: en
  Register #(.width(4)) RDM (.D(R_intr_q), .Q(RDM_q), .clk(clock_2_out), .clr(Reset));  // open: en
  Register register_1 (
    .D(caminho_de_datdos_que_eu_htendi_1_saida_para_o_pc), .Q(register_1_q), .clk(clock_2_out), .clr(Reset));  // open: en
  UC uc_1 (
    .A(R_intr_q_2[4]), .CONT(uc_1_cont), .B(R_intr_q_2[5]), .C(R_intr_q_2[6]), .GRAV(uc_1_grav),
    .B2(uc_1_b2), .MUX1(uc_1_mux1));  // open: MUX2
  Multiplexer #(.width(4), .enable("false")) multiplexer_1 (
    .in0(REM_q), .in1(RDM_q), .out(multiplexer_1_out), .sel(and_1_out));
  and and_1 (and_1_out, 1'b1, uc_1_mux1);
  Caminho_de_datdos_que_eu_htendi caminho_de_datdos_que_eu_htendi_1 (
    .Clock(clock_2_out), .Memori_data({R_intr_q_2, R_intr_q}), .F1(R_intr_q_2[5]), .F0(R_intr_q_2[4]),
    .Seletor_A_B(uc_1_b2), .Saida_para_o_pc(caminho_de_datdos_que_eu_htendi_1_saida_para_o_pc), .Reset(Reset));
  RAM #(.addrWidth(4), .bus("separate")) ram_1 (
    .addr(multiplexer_1_out), .din(register_1_q), .data(ram_1_data), .str(uc_1_grav), .clk(clock_2_out),
    .ld(1'b1));  // open: sel, clr
  Register R_intr (.D(ram_1_data), .Q({R_intr_q_2, R_intr_q}), .clk(clock_2_out), .clr(Reset));  // open: en
endmodule

module ULA (
  input  [7:0] A,
  input  [7:0] B,
  input  F1,
  input  F0,
  output [7:0] out_5
);

  wire [7:0] adder_1_out, multiplier_1_out, subtractor_1_out;

  Adder adder_1 (.a(A), .b(B), .out(adder_1_out));  // open: cin, cout
  Subtractor subtractor_1 (.a(A), .b(B), .out(subtractor_1_out));  // open: bin, bout
  Multiplier multiplier_1 (.a(A), .b(B), .out(multiplier_1_out));  // open: cin, cout
  Multiplexer #(.select(2), .width(8), .enable("false")) multiplexer_1 (
    .in0(adder_1_out), .in1(subtractor_1_out), .in2(multiplier_1_out), .in3({8{1'b0}}), .out(out_5),
    .sel({F1, F0}));
endmodule

module Caminho_de_datdos_que_eu_htendi (
  input  F1,
  input  F0,
  input  [7:0] Memori_data,
  input  Clock,
  input  Seletor_A_B,
  input  Reset,
  output [7:0] Saida_para_o_pc
);

  wire [7:0] A_q, B_q, demultiplexer_1_out0, demultiplexer_1_out1;

  Demultiplexer #(.width(8), .enable("false")) demultiplexer_1 (
    .out0(demultiplexer_1_out0), .out1(demultiplexer_1_out1), .in(Memori_data), .sel(Seletor_A_B));
  Register A (.D(demultiplexer_1_out0), .Q(A_q), .clk(Clock), .clr(Reset));  // open: en
  Register B (.D(demultiplexer_1_out1), .Q(B_q), .clk(Clock), .clr(Reset));  // open: en
  ULA ula_1 (.A(A_q), .B(B_q), .F1(F1), .out_5(Saida_para_o_pc), .F0(F0));
endmodule

module UC (
  input  A,
  input  B,
  input  C,
  output CONT,
  output GRAV,
  output B2,
  output MUX1,
  output MUX2
);

  wire and_3_out, and_4_out, not_1_out, not_2_out, not_3_out, not_4_out, not_5_out, not_6_out;

  not not_1 (not_1_out, A);
  not not_2 (not_2_out, B);
  not not_3 (not_3_out, A);
  not not_4 (not_4_out, B);
  and and_1 (B2, B, C);
  not not_5 (not_5_out, C);
  and and_2 (MUX2, A, C);
  and and_3 (and_3_out, not_1_out, not_2_out);
  not not_6 (not_6_out, C);
  and and_4 (and_4_out, not_3_out, not_4_out);
  and and_5 (MUX1, A, not_5_out);
  and and_6 (CONT, and_3_out, not_6_out);
  and and_7 (GRAV, and_4_out, C);
endmodule

module Decodificador_4bits (
  input  A0,
  input  A1,
  input  A2,
  input  A3,
  output a,
  output b,
  output c,
  output d,
  output e,
  output f,
  output g
);

  wire and_1_out, and_2_out, and_3_out, and_4_out, and_5_out, and_6_out, and_7_out, and_8_out, and_9_out,
       and_10_out, and_11_out, and_12_out, and_13_out, and_14_out, and_15_out, and_16_out, and_17_out,
       and_18_out, and_19_out, and_20_out, and_21_out, and_22_out, and_23_out, and_24_out, and_25_out,
       and_26_out, and_27_out, and_28_out, and_29_out, and_30_out, and_31_out, and_32_out, and_33_out,
       and_34_out, and_35_out, and_36_out, and_37_out, and_38_out, and_39_out, and_40_out, and_41_out,
       and_42_out, and_43_out, and_44_out, and_45_out, and_46_out, and_47_out, not_1_out, not_2_out,
       not_3_out, not_4_out, not_5_out, not_6_out, not_7_out, not_8_out, not_9_out, not_10_out, not_11_out,
       not_12_out, not_13_out, not_14_out, not_15_out, not_16_out, not_17_out, not_18_out, not_19_out,
       not_20_out, not_21_out, not_22_out, not_23_out, not_24_out, not_25_out, not_26_out, not_27_out,
       not_28_out, not_29_out, not_30_out, not_31_out, not_32_out, not_33_out, not_34_out, not_35_out,
       not_36_out, not_37_out, not_38_out, not_39_out, not_40_out, not_41_out, not_42_out, not_43_out,
       not_44_out, or_1_out, or_2_out, or_3_out, or_4_out, or_5_out, or_6_out, or_7_out, or_8_out, or_9_out,
       or_10_out, or_12_out, or_13_out, or_14_out, or_15_out, or_16_out, or_17_out, or_18_out, or_20_out,
       or_21_out, or_22_out, or_23_out;

  not not_1 (not_1_out, A1);
  not not_2 (not_2_out, A3);
  not not_3 (not_3_out, A0);
  not not_4 (not_4_out, A0);
  and and_1 (and_1_out, A0, not_5_out);
  not not_5 (not_5_out, A1);
  not not_6 (not_6_out, A2);
  not not_7 (not_7_out, A0);
  not not_8 (not_8_out, A1);
  not not_9 (not_9_out, A0);
  and and_2 (and_2_out, not_9_out, not_10_out);
  not not_10 (not_10_out, A2);
  not not_11 (not_11_out, A3);
  not not_12 (not_12_out, A0);
  not not_13 (not_13_out, A2);
  not not_14 (not_14_out, A0);
  and and_3 (and_3_out, not_14_out, not_15_out);
  not not_15 (not_15_out, A2);
  not not_16 (not_16_out, A0);
  and and_4 (and_4_out, not_16_out, A3);
  not not_17 (not_17_out, A2);
  not not_18 (not_18_out, A0);
  not not_19 (not_19_out, A1);
  not not_20 (not_20_out, A0);
  and and_5 (and_5_out, not_20_out, not_21_out);
  not not_21 (not_21_out, A1);
  not not_22 (not_22_out, A3);
  not not_23 (not_23_out, A1);
  and and_6 (and_6_out, not_23_out, A2);
  not not_24 (not_24_out, A2);
  not not_25 (not_25_out, A2);
  not not_26 (not_26_out, A1);
  and and_7 (and_7_out, not_26_out, not_27_out);
  not not_27 (not_27_out, A3);
  and and_8 (and_8_out, A2, not_28_out);
  not not_28 (not_28_out, A3);
  and and_9 (and_9_out, A0, A2);
  and and_10 (and_10_out, A0, A1);
  not not_29 (not_29_out, A2);
  not not_30 (not_30_out, A3);
  not not_31 (not_31_out, A0);
  and and_11 (and_11_out, not_31_out, A1);
  not not_32 (not_32_out, A2);
  not not_33 (not_33_out, A1);
  and and_12 (and_12_out, not_33_out, A2);
  and and_13 (and_13_out, A2, not_34_out);
  not not_34 (not_34_out, A3);
  not not_35 (not_35_out, A0);
  and and_14 (and_14_out, not_35_out, A1);
  not not_36 (not_36_out, A2);
  not not_37 (not_37_out, A1);
  and and_15 (and_15_out, not_1_out, not_2_out);
  and and_16 (and_16_out, not_3_out, A2);
  and and_17 (and_17_out, not_4_out, A1);
  and and_18 (and_18_out, A1, A2);
  and and_19 (and_19_out, and_1_out, not_6_out);
  not not_38 (not_38_out, A3);
  and and_20 (and_20_out, not_7_out, not_8_out);
  and and_21 (and_21_out, and_2_out, not_11_out);
  not not_39 (not_39_out, A1);
  not not_40 (not_40_out, A3);
  and and_22 (and_22_out, not_12_out, A2);
  and and_23 (and_23_out, A0, not_13_out);
  or or_1 (or_1_out, and_3_out, and_4_out);
  and and_24 (and_24_out, not_17_out, A3);
  and and_25 (and_25_out, not_18_out, A1);
  and and_26 (and_26_out, A0, not_19_out);
  and and_27 (and_27_out, and_5_out, not_22_out);
  and and_28 (and_28_out, and_6_out, A3);
  and and_29 (and_29_out, A1, not_24_out);
  and and_30 (and_30_out, A1, A2);
  not not_41 (not_41_out, A3);
  and and_31 (and_31_out, A0, not_25_out);
  not not_42 (not_42_out, A3);
  or or_2 (or_2_out, and_7_out, and_8_out);
  or or_3 (or_3_out, and_9_out, and_10_out);
  and and_32 (and_32_out, not_29_out, not_30_out);
  and and_33 (and_33_out, and_11_out, not_32_out);
  not not_43 (not_43_out, A3);
  not not_44 (not_44_out, A1);
  or or_4 (or_4_out, and_12_out, and_13_out);
  and and_34 (and_34_out, and_14_out, not_36_out);
  and and_35 (and_35_out, A0, not_37_out);
  and and_36 (and_36_out, A0, A3);
  or or_5 (or_5_out, and_15_out, and_16_out);
  and and_37 (and_37_out, and_17_out, A3);
  or or_6 (or_6_out, and_18_out, and_19_out);
  and and_38 (and_38_out, A0, not_38_out);
  or or_7 (or_7_out, and_20_out, and_21_out);
  and and_39 (and_39_out, not_39_out, not_40_out);
  and and_40 (and_40_out, and_22_out, A3);
  and and_41 (and_41_out, and_23_out, A3);
  or or_8 (or_8_out, or_1_out, and_24_out);
  or or_9 (or_9_out, and_25_out, and_26_out);
  or or_10 (or_10_out, and_27_out, and_28_out);
  and and_42 (and_42_out, and_29_out, A3);
  and and_43 (and_43_out, and_30_out, not_41_out);
  and and_44 (and_44_out, and_31_out, not_42_out);
  or or_11 (e, or_2_out, or_3_out);
  or or_12 (or_12_out, and_32_out, and_33_out);
  and and_45 (and_45_out, A1, not_43_out);
  and and_46 (and_46_out, A0, not_44_out);
  and and_47 (and_47_out, A0, A2);
  or or_13 (or_13_out, or_4_out, and_34_out);
  or or_14 (or_14_out, and_35_out, and_36_out);
  or or_15 (or_15_out, or_5_out, and_37_out);
  or or_16 (or_16_out, or_6_out, and_38_out);
  or or_17 (or_17_out, or_7_out, and_39_out);
  or or_18 (or_18_out, and_40_out, and_41_out);
  or or_19 (c, or_8_out, or_9_out);
  or or_20 (or_20_out, or_10_out, and_42_out);
  or or_21 (or_21_out, and_43_out, and_44_out);
  or or_22 (or_22_out, or_12_out, and_45_out);
  or or_23 (or_23_out, and_46_out, and_47_out);
  or or_24 (g, or_13_out, or_14_out);
  or or_25 (a, or_15_out, or_16_out);
  or or_26 (b, or_17_out, or_18_out);
  or or_27 (d, or_20_out, or_21_out);
  or or_28 (f, or_22_out, or_23_out);
endmodule

module Caminho_de_dados (
  input  Clear,
  input  Clock,
  input  [7:0] Memori_data,
  input  in_4,
  input  in_5,
  input  in_6,
  input  in_7,
  input  in_8,
  input  in_9,
  input  in_10,
  input  in_11,
  input  _2,
  input  _1,
  input  _0,
  input  BUs_seletor,
  input  in_16,
  output [7:0] out_17,
  output [7:0] Output
);

  wire undriven_2, undriven_3, undriven_4, undriven_5, undriven_6, undriven_7;
  wire [7:0] A_q, B_q, MRB_q, multiplexer_1_out, undriven;

  Register #(.trigger("high")) A (.D(undriven), .en(in_11), .Q(A_q), .clk(Clock), .clr(Clear));
  Register #(.trigger("high")) B (.D(undriven), .en(in_10), .Q(B_q), .clk(Clock), .clr(Clear));
  Register #(.trigger("high")) MRB (.D(Memori_data), .en(in_9), .Q(MRB_q), .clk(Clock), .clr(Clear));
  Register #(.trigger("high")) PC (.D(undriven), .en(in_8), .Q(out_17), .clk(Clock), .clr(Clear));
  Register #(.trigger("high")) u_Output (.D(undriven), .en(in_7), .Q(Output), .clk(Clock), .clr(Clear));
  Multiplexer #(.select(2), .width(8)) multiplexer_1 (
    .in0(B_q), .in1(MRB_q), .in2(out_17), .in3({8{1'b1}}), .out(multiplexer_1_out),
    .sel({BUs_seletor, in_16}), .en(1'b1));
  // ULA ula_1: pin names not known; wires that end beside it: in_4, in_5, in_6
  Multiplexer #(.select(3), .enable("false")) multiplexer_2 (
    .in0(undriven_2), .in1(undriven_3), .in2(undriven_4), .in3(undriven_5), .in4(undriven_6),
    .in5(undriven_7), .in6(1'b0), .in7(1'b0), .sel({_2, _1, _0}));  // open: out
endmodule
